# Fritzing sketch chargeur3v (saved by Fritzing 0.9.3b)
circuit board: 4.25199cm x 5.14877cm
breadboards: 1

parts:
  Q1 = PNP-Transistor [package="TO92 [THT]"]
  C2 = Ceramic Capacitor [capacitance=100nF package="100 mil [THT, multilayer]"]
  23LCV1 = 23LCV1024 [part_number=23LCV1024 package="DIP (Dual Inline) [THT]"]
  LED1 = LED - 5mm [color="Red (633nm)" package="5 mm [THT]"]
  LED2 = LED - 5mm [color="White (4500K)" package="5 mm [THT]"]
  LED3 = LED - 5mm [color="Green (570nm)" package="5 mm [THT]"]
  C3 = Ceramic Capacitor [capacitance=100nF package="100 mil [THT, multilayer]"]
  JP1 = Header 2 [package=molex-1x2_lock]
  JP2 = Header 2 [package=molex-1x2_lock]
  R1 = Resistor [tolerance=±5% resistance=1M package=THT]
  R2 = Resistor [tolerance=±5% resistance=22k package=THT]
  R3 = Resistor [tolerance=±5% resistance=680 package=THT]
  R4 = Resistor [tolerance=±5% resistance=680 package=THT]
  R5 = Resistor [tolerance=±5% resistance=1k package=THT]
  R6 = Resistor [tolerance=±5% resistance=1k package=THT]
  R7 = Resistor [tolerance=±5% resistance=680 package=THT]
  R8 = Resistor [tolerance=±5% resistance=220 package=THT]
  R9 = Resistor [tolerance=±5% resistance=1k package=THT]
  R10 = Resistor [tolerance=±5% resistance=2.2k package=THT]
  R11 = Resistor [tolerance=±5% resistance=2.2k package=THT]

nets:
  N1: Q1.E, 23LCV1.VCC, C3.0, JP1.1, R2.Pin_0, R8.Pin_1
  N2: Q1.B, R7.Pin_1, R8.Pin_0
  N3: Q1.C, JP2.2, R9.Pin_1, R10.Pin_1
  N4: C2.0, 23LCV1.SCK, R1.Pin_1
  N5: C2.1, 23LCV1.VSS, LED2.cathode, LED3.cathode, C3.1, JP1.2, JP2.1, R11.Pin_1
  N6: 23LCV1.CS_, LED1.cathode, R7.Pin_0
  N7: 23LCV1.SO/SIO1, LED3.anode, R9.Pin_0
  N8: 23LCV1.NC, R10.Pin_0, R11.Pin_0
  N9: 23LCV1.SI/SIO0, R3.Pin_0, R4.Pin_1
  N10: 23LCV1.VBAT, R1.Pin_0, R4.Pin_0, R5.Pin_0
  N11: LED1.anode, R5.Pin_1
  N12: LED2.anode, R6.Pin_1
  N13: R2.Pin_1, R3.Pin_1
